# Fritzing sketch LAB GPIO Digital InOut (saved by Fritzing 0.9.3b)
breadboards: 1

parts:
  J1 = STM32 Nucleo boards
  LED1 = smd LED [color="Red (633nm)" package="0805 [SMD]"]
  LED2 = smd LED [color="Red (633nm)" package="0805 [SMD]"]
  LED3 = smd LED [color="Red (633nm)" package="0805 [SMD]"]
  LED4 = smd LED [color="Red (633nm)" package="0805 [SMD]"]
  R1 = Resistor [tolerance=±5% resistance=220 package=THT]
  R2 = Resistor [tolerance=±5% resistance=220 package=THT]
  R3 = Resistor [tolerance=±5% resistance=220 package=THT]
  R4 = Resistor [tolerance=±5% resistance=220 package=THT]

nets:
  N1: J1.GND, R1.Pin_0, R2.Pin_0, R3.Pin_0, R4.Pin_0
  N2: J1.PA5, LED1.anode
  N3: J1.PA6, LED2.anode
  N4: J1.PA7, LED3.anode
  N5: J1.PB6, LED4.anode
  N6: LED1.cathode, R1.Pin_1
  N7: LED2.cathode, R2.Pin_1
  N8: LED3.cathode, R3.Pin_1
  N9: LED4.cathode, R4.Pin_1
